# Fritzing sketch Circuit (saved by Fritzing 1.0.6)
breadboards: 2

parts:
  M1 = DOIT Esp32 DevKit v1 (30 pins long, 11 pins width) [part_number=ESP32S-PIN30]
  IC2 = IC, DIP package, 4 pins [chip_label="AQY212EH PhotoMOS" part_number="AQY212EH PhotoMOS"]
  R1 = Resistor [tolerance=±5% power=0.25W resistance=330 package=THT]
  R2 = Resistor [tolerance=±5% power=0.25W resistance=330 package=THT]
  R3 = Resistor [tolerance=±5% power=0.25W resistance=330 package=THT]
  IC1 = IC, DIP package, 4 pins [chip_label="AQY212EH PhotoMOS" part_number="AQY212EH PhotoMOS"]
  IC3 = IC, DIP package, 4 pins [chip_label="AQY212EH PhotoMOS" part_number="AQY212EH PhotoMOS"]
  Brightness_DOWN = Momentary Switch [package=ksa_sealed_tac_switch]
  Brightness_UP = Momentary Switch [package=ksa_sealed_tac_switch]
  Power = Momentary Switch [package=ksa_sealed_tac_switch]

nets:
  N1: M1.GND, IC2.pin4, IC1.pin4, IC3.pin4
  N2: M1.RX2, R1.Pin_0
  N3: M1.TX2, R2.Pin_0
  N4: M1.D18, R3.Pin_0
  N5: IC2.pin1, Brightness_UP.3
  N6: IC2.pin2, Brightness_UP.1
  N7: IC2.pin3, R2.Pin_1
  N8: R1.Pin_1, IC1.pin3
  N9: R3.Pin_1, IC3.pin3
  N10: IC1.pin1, Brightness_DOWN.3
  N11: IC1.pin2, Brightness_DOWN.1
  N12: IC3.pin1, Power.3
  N13: IC3.pin2, Power.1

notes:
  Power
  Brightness UP
  Brightness DOWN

custom parts:
  DOIT Esp32 DevKit v1 (30 pins long, 11 pins width): The DOIT Esp32 DevKit v1 is one of the development board created by DOIT to evaluate the ESP-WROOM-32 module. It is based on the ESP32 microcontroller that boasts Wifi, Bluetooth, Ethernet and Low Power support all in a single chip. (vanepp) made breadboard work, adjusted pin numbering and labels and reduced size of schematic and cleaned up pcb. This chip is 30pins long (2 x15) and 11 pins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
